// Logisim project lab4circuit.circ as structural Verilog: 1 circuit, main circuit main
module main (
  input  M,
  input  S1,
  input  S0,
  input  Co,
  input  GA,
  input  A0,
  input  B0,
  input  F0,
  input  F1,
  input  F2,
  input  F3,
  input  F4,
  input  Co_2,
  input  A1,
  input  B1,
  input  A2,
  input  B2,
  input  A3,
  input  B3,
  input  A4,
  input  B4
);

  wire and_1_out, and_2_out, and_3_out, and_4_out, and_5_out, and_6_out, and_7_out, and_8_out, and_9_out,
       and_10_out, and_11_out, and_12_out, and_13_out, and_14_out, and_15_out, and_16_out, and_17_out,
       and_18_out, and_19_out, and_20_out, and_21_out, and_22_out, and_23_out, and_24_out, and_25_out,
       and_26_out, and_27_out, and_28_out, multiplexer_1_out, multiplexer_2_out, multiplexer_3_out,
       multiplexer_4_out, multiplexer_5_out, not_1_out, not_2_out, or_1_out, or_2_out, or_3_out, or_4_out,
       or_5_out, or_6_out, or_7_out, or_8_out, or_9_out, or_10_out, or_11_out, or_12_out, or_13_out,
       or_14_out, or_15_out, xnor_1_out, xnor_2_out, xnor_3_out, xnor_4_out, xnor_5_out, xor_1_out,
       xor_2_out, xor_3_out, xor_4_out, xor_5_out, xor_6_out, xor_7_out, xor_8_out, xor_9_out, xor_10_out,
       xor_11_out, xor_12_out, xor_13_out, xor_14_out, xor_15_out, xor_16_out, xor_17_out, xor_18_out,
       xor_19_out, xor_20_out, xor_21_out, xor_22_out, xor_23_out, xor_24_out, xor_25_out;

  not not_1 (not_1_out, M);
  not not_2 (not_2_out, S0);
  and and_1 (and_1_out, not_1_out, Co);
  or or_1 (or_1_out, M, S1, S0);
  and and_2 (and_2_out, not_1_out, S1, not_2_out);
  and and_3 (and_3_out, not_1_out, S1, S0);
  and and_4 (and_4_out, A0, GA);
  and and_5 (and_5_out, B0, or_1_out);
  and and_6 (and_6_out, A0, B0);
  or or_2 (or_2_out, A0, B0);
  xor xor_1 (xor_1_out, A0, B0);
  and and_7 (and_7_out, A1, GA);
  and and_8 (and_8_out, B1, or_1_out);
  and and_9 (and_9_out, A2, GA);
  and and_10 (and_10_out, B2, or_1_out);
  and and_11 (and_11_out, A3, GA);
  and and_12 (and_12_out, B3, or_1_out);
  and and_13 (and_13_out, A4, GA);
  and and_14 (and_14_out, B4, or_1_out);
  xnor xnor_1 (xnor_1_out, A0, B0);
  and and_15 (and_15_out, A1, B1);
  or or_3 (or_3_out, A1, B1);
  xor xor_2 (xor_2_out, A1, B1);
  xnor xnor_2 (xnor_2_out, A1, B1);
  and and_16 (and_16_out, A2, B2);
  or or_4 (or_4_out, A2, B2);
  xor xor_3 (xor_3_out, A2, B2);
  xnor xnor_3 (xnor_3_out, A2, B2);
  and and_17 (and_17_out, A3, B3);
  or or_5 (or_5_out, A3, B3);
  xor xor_4 (xor_4_out, A3, B3);
  xnor xnor_4 (xnor_4_out, A3, B3);
  and and_18 (and_18_out, A4, B4);
  or or_6 (or_6_out, A4, B4);
  xor xor_5 (xor_5_out, A4, B4);
  xnor xnor_5 (xnor_5_out, A4, B4);
  xor xor_6 (xor_6_out, and_4_out, and_3_out);
  xor xor_7 (xor_7_out, and_5_out, and_2_out);
  Multiplexer #(.select(2)) multiplexer_1 (
    .in0(and_6_out), .in1(or_2_out), .in2(xor_1_out), .in3(xnor_1_out), .out(multiplexer_1_out),
    .sel({S1, S0}));  // open: en
  xor xor_8 (xor_8_out, and_7_out, and_3_out);
  xor xor_9 (xor_9_out, and_8_out, and_2_out);
  Multiplexer #(.select(2)) multiplexer_2 (
    .in0(and_15_out), .in1(or_3_out), .in2(xor_2_out), .in3(xnor_2_out), .out(multiplexer_2_out),
    .sel({S1, S0}));  // open: en
  xor xor_10 (xor_10_out, and_9_out, and_3_out);
  xor xor_11 (xor_11_out, and_10_out, and_2_out);
  Multiplexer #(.select(2)) multiplexer_3 (
    .in0(and_16_out), .in1(or_4_out), .in2(xor_3_out), .in3(xnor_3_out), .out(multiplexer_3_out),
    .sel({S1, S0}));  // open: en
  xor xor_12 (xor_12_out, and_11_out, and_3_out);
  xor xor_13 (xor_13_out, and_12_out, and_2_out);
  Multiplexer #(.select(2)) multiplexer_4 (
    .in0(and_17_out), .in1(or_5_out), .in2(xor_4_out), .in3(xnor_4_out), .out(multiplexer_4_out),
    .sel({S1, S0}));  // open: en
  xor xor_14 (xor_14_out, and_13_out, and_3_out);
  xor xor_15 (xor_15_out, and_14_out, and_2_out);
  Multiplexer #(.select(2)) multiplexer_5 (
    .in0(and_18_out), .in1(or_6_out), .in2(xor_5_out), .in3(xnor_5_out), .out(multiplexer_5_out),
    .sel({S1, S0}));  // open: en
  xor xor_16 (xor_16_out, xor_6_out, xor_7_out);
  or or_7 (or_7_out, xor_6_out, xor_7_out);
  and and_19 (and_19_out, xor_6_out, xor_7_out);
  xor xor_17 (xor_17_out, xor_8_out, xor_9_out);
  or or_8 (or_8_out, xor_8_out, xor_9_out);
  and and_20 (and_20_out, xor_8_out, xor_9_out);
  xor xor_18 (xor_18_out, xor_10_out, xor_11_out);
  or or_9 (or_9_out, xor_10_out, xor_11_out);
  and and_21 (and_21_out, xor_10_out, xor_11_out);
  xor xor_19 (xor_19_out, xor_12_out, xor_13_out);
  or or_10 (or_10_out, xor_12_out, xor_13_out);
  and and_22 (and_22_out, xor_12_out, xor_13_out);
  xor xor_20 (xor_20_out, xor_14_out, xor_15_out);
  or or_11 (or_11_out, xor_14_out, xor_15_out);
  and and_23 (and_23_out, xor_14_out, xor_15_out);
  xor xor_21 (xor_21_out, and_1_out, xor_16_out);
  and and_24 (and_24_out, and_1_out, or_7_out);
  xor xor_22 (xor_22_out, or_12_out, xor_17_out);
  and and_25 (and_25_out, or_12_out, or_8_out);
  xor xor_23 (xor_23_out, or_13_out, xor_18_out);
  and and_26 (and_26_out, or_13_out, or_9_out);
  xor xor_24 (xor_24_out, or_14_out, xor_19_out);
  and and_27 (and_27_out, or_14_out, or_10_out);
  xor xor_25 (xor_25_out, or_15_out, xor_20_out);
  and and_28 (and_28_out, or_15_out, or_11_out);
  Multiplexer multiplexer_6 (.in0(xor_21_out), .in1(multiplexer_1_out), .out(F0), .sel(M));  // open: en
  or or_12 (or_12_out, and_24_out, and_19_out);
  Multiplexer multiplexer_7 (.in0(xor_22_out), .in1(multiplexer_2_out), .out(F1), .sel(M));  // open: en
  or or_13 (or_13_out, and_25_out, and_20_out);
  Multiplexer multiplexer_8 (.in0(xor_23_out), .in1(multiplexer_3_out), .out(F2), .sel(M));  // open: en
  or or_14 (or_14_out, and_26_out, and_21_out);
  Multiplexer multiplexer_9 (.in0(xor_24_out), .in1(multiplexer_4_out), .out(F3), .sel(M));  // open: en
  or or_15 (or_15_out, and_27_out, and_22_out);
  Multiplexer multiplexer_10 (.in0(xor_25_out), .in1(multiplexer_5_out), .out(F4), .sel(M));  // open: en
  or or_16 (Co_2, and_28_out, and_23_out);

  // Notes on the sheet:
  //   Cin
  //   GB
  //   FB
  //   FA
endmodule
