// Logisim project segment.circ as structural Verilog: 1 circuit, main circuit main
module main (
  input  _0,
  input  _1,
  input  _2,
  input  _3,
  input  _4,
  input  _5,
  input  _6,
  input  _7,
  input  _8,
  input  _9,
  output A,
  output B,
  output C,
  output D,
  output E,
  output F,
  output G
);

  wire A_C_out, A_out, B_out, B_prime_C_out, B_prime_D_prime_out, BC_prime_D_out, BC_prime_out, BD_out,
       BD_prime_out, C_out, C_prime_D_prime_out, CD_out, CD_prime_out, D_C_prime_out, D_out, not_1_out,
       not_2_out, not_3_out, not_4_out, or_1_out, or_2_out, or_3_out, or_4_out, or_5_out;

  not not_1 (not_1_out, A_out);
  or u_A (A_out, _8, _9);
  not not_2 (not_2_out, B_out);
  or u_B (B_out, _4, _5, _6, _7);
  not not_3 (not_3_out, C_out);
  or u_C (C_out, _2, _3, _6, _7);
  not not_4 (not_4_out, D_out);
  or u_D (D_out, _1, _3, _5, _7, _9);
  and BD (BD_out, B_out, D_out);
  and B_prime_D_prime (B_prime_D_prime_out, not_2_out, not_4_out);
  and CD (CD_out, C_out, D_out);
  and C_prime_D_prime (C_prime_D_prime_out, not_3_out, not_4_out);
  or D_C_prime (D_C_prime_out, not_3_out, D_out);
  or or_1 (or_1_out, CD_out, C_prime_D_prime_out);
  or or_2 (or_2_out, BD_out, B_prime_D_prime_out);
  or A_C (A_C_out, A_out, C_out);
  and CD_prime (CD_prime_out, C_out, not_4_out);
  and B_prime_C (B_prime_C_out, not_2_out, C_out);
  and BC_prime_D (BC_prime_D_out, B_out, not_3_out, D_out);
  and BD_prime (BD_prime_out, B_out, not_4_out);
  and BC_prime (BC_prime_out, B_out, not_3_out);
  or or_3 (or_3_out, CD_prime_out, B_prime_C_out, BC_prime_D_out, B_prime_D_prime_out);
  or or_4 (or_4_out, C_prime_D_prime_out, BD_prime_out, BC_prime_out);
  or or_5 (or_5_out, B_prime_C_out, BD_prime_out, BC_prime_out);
  or or_6 (A, or_2_out, A_C_out);
  or or_7 (B, not_2_out, or_1_out);
  or or_8 (C, B_out, D_C_prime_out);
  or or_9 (D, A_out, or_3_out);
  or or_10 (E, CD_prime_out, B_prime_D_prime_out);
  or or_11 (F, A_out, or_4_out);
  or or_12 (G, A_out, or_5_out);
endmodule
